# Fritzing sketch POC Wiring (saved by Fritzing 0.9.4)
circuit board: 8.46667cm x 5.64444cm
breadboards: 1

parts:
  R1 = Resistor [tolerance=±5% resistance=220 package=THT]
  Composant1 = Arduino Uno (Rev3)

nets:
  N1: R1.Pin_0, Composant1.D1/TX
  N2: R1.Pin_1, Composant1.RESET
